// Logisim project ALU.circ as structural Verilog
module alu (
  input  [3:0] A,
  input  [3:0] B,
  input  [1:0] ALUOp,
  output [3:0] C
);

  wire [3:0] C0, C1, C2, C3;

  Adder #(.width(4)) adder_1 (.a(A), .b(B), .out(C0));  // open: cin, cout
  assign C2 = A & B;  // AND_Gate and_1, 4 bits wide
  Multiplexer #(.select(2), .width(4)) multiplexer_1 (
    .in0(C0), .in1(C1), .in2(C2), .in3(C3), .out(C), .sel(ALUOp));  // open: en
  Subtractor #(.width(4)) subtractor_1 (.a(A), .b(B), .out(C1));  // open: bin, bout
  assign C3 = A | B;  // OR_Gate or_1, 4 bits wide
endmodule
