// Logisim project CRC.circ as structural Verilog
module _4bit (
  input  [3:0] A,
  input  [3:0] B,
  output q,
  output [3:0] r
);

  wire [3:0] xor_1_out;

  assign xor_1_out = A ^ B;  // XOR_Gate xor_1, 4 bits wide
  Multiplexer multiplexer_1 (.in0(1'b0), .in1(1'b1), .out(q), .sel(A[3]));  // open: en
  Multiplexer #(.width(4)) multiplexer_2 (.in0(A), .in1({1'b0, xor_1_out[2:0]}), .out(r), .sel(A[3]));  // open: en
endmodule

module CRC (
  input  [7:0] A,
  input  [3:0] B,
  output [10:0] C
);

  wire q0, q1, q2, q3, q4, q5, q6, q7;
  wire [3:0] r0, r1, r2, r3, r4, r5, r6;
  wire [3:3] r7;

  _4bit u_4bit_1 (.A(A[7:4]), .B(B), .q(q0), .r(r0));
  _4bit u_4bit_2 (.A({r0[2:0], A[3]}), .B(B), .q(q1), .r(r1));
  _4bit u_4bit_3 (.A({r1[2:0], A[2]}), .B(B), .q(q2), .r(r2));
  _4bit u_4bit_4 (.A({r2[2:0], A[1]}), .B(B), .q(q3), .r(r3));
  _4bit u_4bit_5 (.A({r3[2:0], A[0]}), .B(B), .q(q4), .r(r4));
  _4bit u_4bit_6 (.A({r4[2:0], 1'b0}), .B(B), .q(q5), .r(r5));
  _4bit u_4bit_7 (.A({r5[2:0], 1'b0}), .B(B), .q(q6), .r(r6));
  _4bit u_4bit_8 (.A({r6[2:0], 1'b0}), .B(B), .q(q7), .r({r7[3], C[2:0]}));

  assign C[10:3] = A;

  // Other names for the same wires on the sheet: r7[2:0] = C[2:0]
endmodule
