// Logisim project GRF.circ as structural Verilog
module GRF (
  input  WE,
  input  reset,
  input  clk,
  input  [31:0] WD,
  input  [4:0] A3,
  input  [4:0] RA1,
  input  [4:0] RA2,
  output [31:0] RD1,
  output [31:0] RD2
);

  wire [31:0] _1, _2, _3, _4, _5, _6, _7, _8, _9, _10, _11, _12, _13, _14, _15, _16, _17, _18, _19, _20, _21,
       _22, _23, _24, _25, _26, _27, _28, _29, _30, _31, i0, i1, i2, i3, i4, i5, i6, i7, i8, i9, i10, i11,
       i12, i13, i14, i15, i16, i17, i18, i19, i20, i21, i22, i23, i24, i25, i26, i27, i28, i29, i30, i31;

  Register #(.width(32)) _0 (.D(i0), .en(WE), .clk(clk), .clr(reset));  // open: Q
  Register #(.width(32)) u__8 (.D(i8), .en(WE), .Q(_8), .clk(clk), .clr(reset));
  Register #(.width(32)) u__16 (.D(i16), .en(WE), .Q(_16), .clk(clk), .clr(reset));
  Register #(.width(32)) u__24 (.D(i24), .en(WE), .Q(_24), .clk(clk), .clr(reset));
  Register #(.width(32)) u__1 (.D(i1), .en(WE), .Q(_1), .clk(clk), .clr(reset));
  Register #(.width(32)) u__9 (.D(i9), .en(WE), .Q(_9), .clk(clk), .clr(reset));
  Register #(.width(32)) u__17 (.D(i17), .en(WE), .Q(_17), .clk(clk), .clr(reset));
  Register #(.width(32)) u__25 (.D(i25), .en(WE), .Q(_25), .clk(clk), .clr(reset));
  Register #(.width(32)) u__2 (.D(i2), .en(WE), .Q(_2), .clk(clk), .clr(reset));
  Register #(.width(32)) u__10 (.D(i10), .en(WE), .Q(_10), .clk(clk), .clr(reset));
  Register #(.width(32)) u__18 (.D(i18), .en(WE), .Q(_18), .clk(clk), .clr(reset));
  Register #(.width(32)) u__26 (.D(i26), .en(WE), .Q(_26), .clk(clk), .clr(reset));
  Multiplexer #(.select(5), .width(32)) multiplexer_1 (
    .in0({32{1'b0}}), .in1(_1), .in2(_2), .in3(_3), .in4(_4), .in5(_5), .in6(_6), .in7(_7), .in8(_8),
    .in9(_9), .in10(_10), .in11(_11), .in12(_12), .in13(_13), .in14(_14), .in15(_15), .in16(_16), .in17(_17),
    .in18(_18), .in19(_19), .in20(_20), .in21(_21), .in22(_22), .in23(_23), .in24(_24), .in25(_25),
    .in26(_26), .in27(_27), .in28(_28), .in29(_29), .in30(_30), .in31(_31), .out(RD1), .sel(RA1));  // open: en
  Register #(.width(32)) u__3 (.D(i3), .en(WE), .Q(_3), .clk(clk), .clr(reset));
  Register #(.width(32)) u__11 (.D(i11), .en(WE), .Q(_11), .clk(clk), .clr(reset));
  Register #(.width(32)) u__19 (.D(i19), .en(WE), .Q(_19), .clk(clk), .clr(reset));
  Register #(.width(32)) u__27 (.D(i27), .en(WE), .Q(_27), .clk(clk), .clr(reset));
  Register #(.width(32)) u__4 (.D(i4), .en(WE), .Q(_4), .clk(clk), .clr(reset));
  Register #(.width(32)) u__12 (.D(i12), .en(WE), .Q(_12), .clk(clk), .clr(reset));
  Register #(.width(32)) u__20 (.D(i20), .en(WE), .Q(_20), .clk(clk), .clr(reset));
  Register #(.width(32)) u__28 (.D(i28), .en(WE), .Q(_28), .clk(clk), .clr(reset));
  Register #(.width(32)) u__5 (.D(i5), .en(WE), .Q(_5), .clk(clk), .clr(reset));
  Register #(.width(32)) u__13 (.D(i13), .en(WE), .Q(_13), .clk(clk), .clr(reset));
  Register #(.width(32)) u__21 (.D(i21), .en(WE), .Q(_21), .clk(clk), .clr(reset));
  Register #(.width(32)) u__29 (.D(i29), .en(WE), .Q(_29), .clk(clk), .clr(reset));
  Register #(.width(32)) u__6 (.D(i6), .en(WE), .Q(_6), .clk(clk), .clr(reset));
  Register #(.width(32)) u__14 (.D(i14), .en(WE), .Q(_14), .clk(clk), .clr(reset));
  Register #(.width(32)) u__22 (.D(i22), .en(WE), .Q(_22), .clk(clk), .clr(reset));
  Register #(.width(32)) u__30 (.D(i30), .en(WE), .Q(_30), .clk(clk), .clr(reset));
  Multiplexer #(.select(5), .width(32)) multiplexer_2 (
    .in0({32{1'b0}}), .in1(_1), .in2(_2), .in3(_3), .in4(_4), .in5(_5), .in6(_6), .in7(_7), .in8(_8),
    .in9(_9), .in10(_10), .in11(_11), .in12(_12), .in13(_13), .in14(_14), .in15(_15), .in16(_16), .in17(_17),
    .in18(_18), .in19(_19), .in20(_20), .in21(_21), .in22(_22), .in23(_23), .in24(_24), .in25(_25),
    .in26(_26), .in27(_27), .in28(_28), .in29(_29), .in30(_30), .in31(_31), .out(RD2), .sel(RA2));  // open: en
  Register #(.width(32)) u__7 (.D(i7), .en(WE), .Q(_7), .clk(clk), .clr(reset));
  Register #(.width(32)) u__15 (.D(i15), .en(WE), .Q(_15), .clk(clk), .clr(reset));
  Register #(.width(32)) u__23 (.D(i23), .en(WE), .Q(_23), .clk(clk), .clr(reset));
  Register #(.width(32)) u__31 (.D(i31), .en(WE), .Q(_31), .clk(clk), .clr(reset));
  Demultiplexer #(.select(5), .width(32), .tristate("true")) demultiplexer_1 (
    .out0(i0), .out1(i1), .out2(i2), .out3(i3), .out4(i4), .out5(i5), .out6(i6), .out7(i7), .out8(i8),
    .out9(i9), .out10(i10), .out11(i11), .out12(i12), .out13(i13), .out14(i14), .out15(i15), .out16(i16),
    .out17(i17), .out18(i18), .out19(i19), .out20(i20), .out21(i21), .out22(i22), .out23(i23), .out24(i24),
    .out25(i25), .out26(i26), .out27(i27), .out28(i28), .out29(i29), .out30(i30), .out31(i31), .in(WD),
    .sel(A3));  // open: en
endmodule
