// Logisim project fsm_正则匹配.circ as structural Verilog
module fsm (
  input  [1:0] In,
  input  CLR,
  output Z
);

  wire CLK_out, register_2_q;
  wire [1:0] register_1_q, state_transition_1_out_state;

  state_transition state_transition_1 (.In(In), .in_state(register_1_q), .out_state(state_transition_1_out_state));
  Clock CLK (.out(CLK_out));
  Register #(.width(2)) register_1 (
    .D(state_transition_1_out_state), .Q(register_1_q), .clk(CLK_out), .clr(register_2_q));  // open: en
  Register #(.width(1)) register_2 (.D(CLR), .Q(register_2_q), .clk(CLK_out), .clr(register_2_q));  // open: en
  state_output state_output_1 (.In(In), .state(register_1_q), .Z(Z));
endmodule

module state_transition (
  input  [1:0] In,
  input  [1:0] in_state,
  output [1:0] out_state
);

  wire and_1_out, and_2_out, and_3_out, and_4_out, and_5_out, not_1_out, not_2_out, not_3_out, not_4_out,
       not_5_out, not_6_out, not_7_out, not_8_out, not_9_out;

  not not_1 (not_1_out, In[0]);
  not not_2 (not_2_out, in_state[0]);
  not not_3 (not_3_out, In[0]);
  not not_4 (not_4_out, in_state[1]);
  and and_1 (and_1_out, not_1_out, not_2_out, in_state[1]);
  and and_2 (and_2_out, not_3_out, in_state[0], not_4_out);
  or or_1 (out_state[1], and_1_out, and_2_out);
  not not_5 (not_5_out, In[1]);
  not not_6 (not_6_out, in_state[0]);
  not not_7 (not_7_out, In[0]);
  not not_8 (not_8_out, in_state[0]);
  not not_9 (not_9_out, In[1]);
  and and_3 (and_3_out, not_5_out, not_6_out, in_state[1]);
  and and_4 (and_4_out, not_7_out, not_8_out, in_state[1]);
  and and_5 (and_5_out, In[0], not_9_out);
  or or_2 (out_state[0], and_3_out, and_4_out, and_5_out);

  // Other names for the same wires on the sheet: A1 = In[0]; A2 = In[1]; A3 = in_state[0]; A4 = in_state[1];
  //   S0 = out_state[0]; S1 = out_state[1]
endmodule

module state_output (
  input  [1:0] In,
  input  [1:0] state,
  output Z
);

  wire not_1_out, not_2_out;

  not not_1 (not_1_out, In[0]);
  not not_2 (not_2_out, state[0]);
  and and_1 (Z, not_1_out, not_2_out, state[1]);

  // Other names for the same wires on the sheet: A1 = In[0]; A2 = In[1]; A3 = state[0]; A4 = state[1]
endmodule
