// Logisim project P3-CPU.circ as structural Verilog: 9 circuits, main circuit main
module main (
  input  Reset
);

  wire alu_1_equal, ALUSrc, CLK_out, if_swl, MemRead, MemWrite, RegWrite;
  wire [1:0] alu_controller_1_out_3, ALUOp, Branch, Extend, MemtoReg, RegDst;
  wire [4:0] adder_1_out, branch_1_npc, branch_1_pc_4, ifu_1_pc_out, MemAddr, multiplexer_1_out;
  wire [31:0] alu_1_result, bit_extender_1_out, ext_1_ext, ifu_1_instr, MemData, multiplexer_2_out,
       multiplexer_3_out, multiplexer_4_out, ram_1_data, register_file_1_rd1, swl_calculator_1_out_3;

  Clock CLK (.out(CLK_out));
  IFU ifu_1 (.NextPC(branch_1_npc), .CLK(CLK_out), .Reset(Reset), .PC_out(ifu_1_pc_out), .Instr(ifu_1_instr));
  Controller controller_1 (
    .Op0(ifu_1_instr[26]), .Op1(ifu_1_instr[27]), .Op2(ifu_1_instr[28]), .Op3(ifu_1_instr[29]),
    .Op4(ifu_1_instr[30]), .Op5(ifu_1_instr[31]), .RegDst(RegDst), .Branch(Branch), .MemtoReg(MemtoReg),
    .MemWrite(MemWrite), .MemRead(MemRead), .ALUOp(ALUOp), .ALUSrc(ALUSrc), .RegWrite(RegWrite),
    .Extend(Extend), .if_swl(if_swl));
  Adder #(.width(5)) adder_1 (.a(ifu_1_pc_out), .b(5'b00001), .out(adder_1_out));  // open: cin, cout
  Multiplexer #(.select(2), .width(5)) multiplexer_1 (
    .in0(ifu_1_instr[20:16]), .in1(ifu_1_instr[15:11]), .in2({5{1'b1}}), .out(multiplexer_1_out), .sel(RegDst));  // open: in3, en
  EXT ext_1 (.imm(ifu_1_instr[15:0]), .Extend(Extend), .ext(ext_1_ext));
  Register_File register_file_1 (
    .RA1(ifu_1_instr[25:21]), .RA2(ifu_1_instr[20:16]), .WD(multiplexer_4_out), .WA(multiplexer_1_out),
    .RD1(register_file_1_rd1), .RD2(MemData), .CLK(CLK_out), .RegWrite(RegWrite));
  Multiplexer #(.width(32)) multiplexer_2 (
    .in0(MemData), .in1(ext_1_ext), .out(multiplexer_2_out), .sel(ALUSrc));  // open: en
  ALU alu_1 (
    .A(register_file_1_rd1), .B(multiplexer_2_out),
    .Result({alu_1_result[31:7], MemAddr, alu_1_result[1:0]}), .Equal(alu_1_equal),
    .ALUCtrl(alu_controller_1_out_3));
  ALU_Controller alu_controller_1 (.ALUOp(ALUOp), .Funct(ifu_1_instr[5:0]), .out_3(alu_controller_1_out_3));
  Branch branch_1 (
    .PC(adder_1_out), .imme(ext_1_ext[4:0]), .Branch(Branch), .Equal(alu_1_equal), .NPC(branch_1_npc),
    .PC_4(branch_1_pc_4));
  swl_calculator swl_calculator_1 (.n(alu_1_result[1:0]), .RT(MemData), .out_3(swl_calculator_1_out_3));
  assign bit_extender_1_out = {{27{branch_1_pc_4[4]}}, branch_1_pc_4};  // Bit_Extender bit_extender_1
  Multiplexer #(.width(32)) multiplexer_3 (
    .in0(MemData), .in1(swl_calculator_1_out_3), .out(multiplexer_3_out), .sel(if_swl));  // open: en
  RAM #(.addrWidth(5), .dataWidth(32), .bus("separate")) ram_1 (
    .addr(MemAddr), .din(multiplexer_3_out), .data(ram_1_data), .str(MemWrite), .clk(CLK_out), .ld(MemRead));  // open: sel, clr
  Multiplexer #(.select(2), .width(32)) multiplexer_4 (
    .in0(ram_1_data), .in1({alu_1_result[31:7], MemAddr, alu_1_result[1:0]}), .in2(ext_1_ext),
    .in3(bit_extender_1_out), .out(multiplexer_4_out), .sel(MemtoReg));  // open: en
endmodule

module Controller (
  input  Op0,
  input  Op1,
  input  Op2,
  input  Op3,
  input  Op4,
  input  Op5,
  output [1:0] RegDst,
  output [1:0] Branch,
  output [1:0] MemtoReg,
  output MemWrite,
  output MemRead,
  output [1:0] ALUOp,
  output ALUSrc,
  output RegWrite,
  output [1:0] Extend,
  output if_swl
);

  wire not_1_out, not_2_out, not_3_out, not_4_out, not_5_out, not_6_out, sw_out;

  not not_1 (not_1_out, Op0);
  not not_2 (not_2_out, Op1);
  not not_3 (not_3_out, Op2);
  not not_4 (not_4_out, Op3);
  not not_5 (not_5_out, Op4);
  not not_6 (not_6_out, Op5);
  and R (ALUOp[0], not_6_out, not_5_out, not_4_out, not_3_out, not_2_out, not_1_out);
  and lw (MemRead, Op5, not_5_out, not_4_out, not_3_out, Op1, Op0);
  and sw (sw_out, Op5, not_5_out, Op3, not_3_out, Op1, Op0);
  and beq (Branch[0], not_6_out, not_5_out, not_4_out, Op2, not_2_out, not_1_out);
  and ori (Extend[0], not_6_out, not_5_out, Op3, Op2, not_2_out, Op0);
  and lui (Extend[1], not_6_out, not_5_out, Op3, Op2, Op1, Op0);
  and swl (if_swl, Op5, not_5_out, Op3, not_3_out, Op1, not_1_out);
  and jal (Branch[1], not_6_out, not_5_out, not_4_out, not_3_out, Op1, Op0);
  or or_1 (MemtoReg[1], Branch[1], Extend[1]);
  or or_2 (MemtoReg[0], ALUOp[0], Branch[1], Extend[0]);
  or or_3 (MemWrite, sw_out, if_swl);
  or or_4 (ALUOp[1], Extend[0], ALUOp[0]);
  or or_5 (ALUSrc, MemRead, if_swl, sw_out, Extend[0]);
  or or_6 (RegWrite, ALUOp[0], MemRead, Extend[0], Extend[1]);

  assign RegDst = {Branch[1], ALUOp[0]};
endmodule

module ALU_Controller (
  input  [1:0] ALUOp,
  input  [5:0] Funct,
  output [1:0] out_3
);

  wire not_1_out, not_2_out, not_3_out, not_4_out;

  not not_1 (not_1_out, Funct[2]);
  not not_2 (not_2_out, Funct[3]);
  not not_3 (not_3_out, Funct[4]);
  not not_4 (not_4_out, ALUOp[0]);
  and and_1 (out_3[1], not_4_out, ALUOp[1]);
  and and_2 (out_3[0], ALUOp[0], ALUOp[1], Funct[0], Funct[1], not_1_out, not_2_out, not_3_out, Funct[5]);
endmodule

module IFU (
  input  [4:0] NextPC,
  input  CLK,
  input  Reset,
  output [4:0] PC_out,
  output [31:0] Instr
);

  Register #(.width(5)) PC (.D(NextPC), .Q(PC_out), .clk(CLK), .clr(Reset));  // open: en
  ROM #(.addrWidth(5), .dataWidth(32)) rom_1 (.addr(PC_out), .data(Instr));  // open: sel

  // Notes on the sheet:
  //   contents of rom_1 (hex, n*v repeats v):
  //   3c00a234 3c010001 3c020002 3c030003 3c040004 3c050006 3c06001a 3c07002d 3c081000 3c09a6b3 3c0a9999
  //   3c0b0ff2 3c0ca222 3c0dbad3 3c0e4323 3c0f9876 3c10b678 3c112345 3c12a123 3c13a345 3c140001 3c159a2a
  //   3c16bbbb 3c17cccc 3c18dddd 3c19ffff 3c1aee22 3c1b22ee 3c1cabcd 3c1ddcb3 3c1e3cda 3c1fffff
endmodule

module ALU (
  input  [31:0] A,
  input  [31:0] B,
  input  [1:0] ALUCtrl,
  output [31:0] Result,
  output Equal
);

  wire [31:0] adder_1_out, and_1_out, or_1_out, subtractor_1_out;

  Adder #(.width(32)) adder_1 (.a(A), .b(B), .out(adder_1_out));  // open: cin, cout
  Subtractor #(.width(32)) subtractor_1 (.a(A), .b(B), .out(subtractor_1_out));  // open: bin, bout
  assign or_1_out = A | B;  // OR_Gate or_1, 32 bits wide
  assign and_1_out = A & B;  // AND_Gate and_1, 32 bits wide
  Comparator #(.width(32), .mode("unsigned")) comparator_1 (.a(A), .b(B), .eq(Equal));  // open: gt, lt
  Multiplexer #(.select(2), .width(32)) multiplexer_1 (
    .in0(adder_1_out), .in1(subtractor_1_out), .in2(or_1_out), .in3(and_1_out), .out(Result), .sel(ALUCtrl));  // open: en
endmodule

module Register_File (
  input  [4:0] RA1,
  input  [4:0] RA2,
  input  [31:0] WD,
  input  [4:0] WA,
  input  CLK,
  input  RegWrite,
  output [31:0] RD1,
  output [31:0] RD2
);

  wire undriven, undriven_2, undriven_3, undriven_4;
  wire [31:0] i1, i2, i3, i4, i5, i6, i7, i8, i9, i10, i11, i12, i13, i14, i15, i16, i17, i18, i19, i20, i21,
       i22, i23, i24, i25, i26, i27, i28, i29, i30, i31, o1, o2, o3, o4, o5, o6, o7, o8, o9, o10, o11, o12,
       o13, o14, o15, o16, o17, o18, o19, o20, o21, o22, o23, o24, o25, o26, o27, o28, o29, o30, o31;

  Register #(.width(32)) _0 (.en(RegWrite), .clk(CLK), .clr(undriven));  // open: D, Q
  Register #(.width(32)) _8 (.D(i8), .en(RegWrite), .Q(o8), .clk(CLK), .clr(undriven_2));
  Register #(.width(32)) _16 (.D(i16), .en(RegWrite), .Q(o16), .clk(CLK), .clr(undriven_3));
  Register #(.width(32)) _24 (.D(i24), .en(RegWrite), .Q(o24), .clk(CLK), .clr(undriven_4));
  Demultiplexer #(.select(5), .width(32), .tristate("true")) demultiplexer_1 (
    .out1(i1), .out2(i2), .out3(i3), .out4(i4), .out5(i5), .out6(i6), .out7(i7), .out8(i8), .out9(i9),
    .out10(i10), .out11(i11), .out12(i13), .out13(i12), .out14(i14), .out15(i15), .out16(i16), .out17(i17),
    .out18(i18), .out19(i19), .out20(i20), .out21(i21), .out22(i22), .out23(i23), .out24(i24), .out25(i25),
    .out26(i26), .out27(i27), .out28(i28), .out29(i29), .out30(i30), .out31(i31), .in(WD), .sel(WA));  // open: out0, en
  Register #(.width(32)) _1 (.D(i1), .en(RegWrite), .Q(o1), .clk(CLK));  // open: clr
  Register #(.width(32)) _9 (.D(i9), .en(RegWrite), .Q(o9), .clk(CLK));  // open: clr
  Register #(.width(32)) _17 (.D(i17), .en(RegWrite), .Q(o17), .clk(CLK));  // open: clr
  Register #(.width(32)) _25 (.D(i25), .en(RegWrite), .Q(o25), .clk(CLK));  // open: clr
  Register #(.width(32)) _2 (.D(i2), .en(RegWrite), .Q(o2), .clk(CLK));  // open: clr
  Register #(.width(32)) _10 (.D(i10), .en(RegWrite), .Q(o10), .clk(CLK));  // open: clr
  Register #(.width(32)) _18 (.D(i18), .en(RegWrite), .Q(o18), .clk(CLK));  // open: clr
  Register #(.width(32)) _26 (.D(i26), .en(RegWrite), .Q(o26), .clk(CLK));  // open: clr
  Multiplexer #(.select(5), .width(32)) multiplexer_1 (
    .in0({32{1'b0}}), .in1(o1), .in2(o2), .in3(o3), .in4(o4), .in5(o5), .in6(o6), .in7(o7), .in8(o8),
    .in9(o9), .in10(o10), .in11(o11), .in12(o12), .in13(o13), .in14(o14), .in15(o15), .in16(o16), .in17(o17),
    .in18(o18), .in19(o19), .in20(o20), .in21(o21), .in22(o22), .in23(o23), .in24(o24), .in25(o25),
    .in26(o26), .in27(o27), .in28(o28), .in29(o29), .in30(o30), .in31(o31), .out(RD1), .sel(RA1));  // open: en
  Register #(.width(32)) _3 (.D(i3), .en(RegWrite), .Q(o3), .clk(CLK));  // open: clr
  Register #(.width(32)) _11 (.D(i11), .en(RegWrite), .Q(o11), .clk(CLK));  // open: clr
  Register #(.width(32)) _19 (.D(i19), .en(RegWrite), .Q(o19), .clk(CLK));  // open: clr
  Register #(.width(32)) _27 (.D(i27), .en(RegWrite), .Q(o27), .clk(CLK));  // open: clr
  Multiplexer #(.select(5), .width(32)) multiplexer_2 (
    .in0({32{1'b0}}), .in1(o1), .in2(o2), .in3(o3), .in4(o4), .in5(o5), .in6(o6), .in7(o7), .in8(o8),
    .in9(o9), .in10(o10), .in11(o11), .in12(o12), .in13(o13), .in14(o14), .in15(o15), .in16(o16), .in17(o17),
    .in18(o18), .in19(o19), .in20(o20), .in21(o21), .in22(o22), .in23(o23), .in24(o24), .in25(o25),
    .in26(o26), .in27(o27), .in28(o28), .in29(o29), .in30(o30), .in31(o31), .out(RD2), .sel(RA2));  // open: en
  Register #(.width(32)) _4 (.D(i4), .en(RegWrite), .Q(o4), .clk(CLK));  // open: clr
  Register #(.width(32)) _12 (.D(i12), .en(RegWrite), .Q(o12), .clk(CLK));  // open: clr
  Register #(.width(32)) _20 (.D(i20), .en(RegWrite), .Q(o20), .clk(CLK));  // open: clr
  Register #(.width(32)) _28 (.D(i28), .en(RegWrite), .Q(o28), .clk(CLK));  // open: clr
  Register #(.width(32)) _5 (.D(i5), .en(RegWrite), .Q(o5), .clk(CLK));  // open: clr
  Register #(.width(32)) _13 (.D(i13), .en(RegWrite), .Q(o13), .clk(CLK));  // open: clr
  Register #(.width(32)) _21 (.D(i21), .en(RegWrite), .Q(o21), .clk(CLK));  // open: clr
  Register #(.width(32)) _29 (.D(i29), .en(RegWrite), .Q(o29), .clk(CLK));  // open: clr
  Register #(.width(32)) _6 (.D(i6), .en(RegWrite), .Q(o6), .clk(CLK));  // open: clr
  Register #(.width(32)) _14 (.D(i14), .en(RegWrite), .Q(o14), .clk(CLK));  // open: clr
  Register #(.width(32)) _22 (.D(i22), .en(RegWrite), .Q(o22), .clk(CLK));  // open: clr
  Register #(.width(32)) _30 (.D(i30), .en(RegWrite), .Q(o30), .clk(CLK));  // open: clr
  Register #(.width(32)) _7 (.D(i7), .en(RegWrite), .Q(o7), .clk(CLK));  // open: clr
  Register #(.width(32)) _15 (.D(i15), .en(RegWrite), .Q(o15), .clk(CLK));  // open: clr
  Register #(.width(32)) _23 (.D(i23), .en(RegWrite), .Q(o23), .clk(CLK));  // open: clr
  Register #(.width(32)) _31 (.D(i31), .en(RegWrite), .Q(o31), .clk(CLK));  // open: clr
endmodule

module EXT (
  input  [15:0] imm,
  input  [1:0] Extend,
  output [31:0] ext
);

  wire [31:0] bit_extender_1_out, bit_extender_2_out;

  assign bit_extender_1_out = {{16{imm[15]}}, imm};  // Bit_Extender bit_extender_1
  assign bit_extender_2_out = {{16{1'b0}}, imm};  // Bit_Extender bit_extender_2
  Multiplexer #(.select(2), .width(32)) multiplexer_1 (
    .in0(bit_extender_1_out), .in1(bit_extender_2_out), .in2({imm, {16{1'b0}}}), .out(ext), .sel(Extend));  // open: in3, en
endmodule

module swl_calculator (
  input  [1:0] n,
  input  [31:0] RT,
  output [31:0] out_3
);

  Multiplexer #(.select(2), .width(32)) multiplexer_1 (
    .in0(RT), .in1({{8{1'b0}}, RT[31:8]}), .in2({{16{1'b0}}, RT[31:16]}), .in3({{24{1'b0}}, RT[31:24]}),
    .out(out_3), .sel(n));  // open: en

  // Other names for the same wires on the sheet: _0[7:0] = RT[7:0]; _1[7:0] = RT[15:8]; _3[7:0] = RT[31:24];
  //   _2[7:0] = RT[23:16]
endmodule

module Branch (
  input  [4:0] PC,
  input  [4:0] imme,
  input  [1:0] Branch,
  input  Equal,
  output [4:0] NPC,
  output [4:0] PC_4
);

  wire [0:0] and_1_out;
  wire [4:0] adder_1_out;

  Adder #(.width(5)) adder_1 (.a(PC), .b(imme), .out(adder_1_out));  // open: cin, cout
  and and_1 (and_1_out[0], Branch[0], Equal);
  Multiplexer #(.select(2), .width(5)) multiplexer_1 (
    .in0(PC), .in1(adder_1_out), .in2({PC[4:1], imme[0]}), .out(NPC), .sel({Branch[1], and_1_out[0]}));  // open: in3, en

  assign PC_4 = PC;
endmodule
