// Logisim project mode5.circ as structural Verilog
module mod5 (
  input  In,
  output S0,
  output S1,
  output S2,
  output S3,
  output S4
);

  wire clock_1_out;
  wire [4:0] register_1_q;

  state state_1 (.in_1(register_1_q), .in_2(In), .out_3({S4, S3, S2, S1, S0}));
  Clock clock_1 (.out(clock_1_out));
  Register #(.width(5)) register_1 (.D({S4, S3, S2, S1, S0}), .Q(register_1_q), .clk(clock_1_out));  // open: en, clr
endmodule

module state (
  input  [4:0] in_1,
  input  in_2,
  output [4:0] out_3
);

  wire and_1_out, and_2_out, and_3_out, and_4_out, and_5_out, and_6_out, and_7_out, and_8_out, and_9_out,
       and_10_out, not_1_out, not_2_out, not_3_out, not_4_out, not_5_out, not_6_out, not_7_out, not_8_out,
       not_9_out, not_10_out, not_11_out, not_12_out, not_13_out, not_14_out, not_15_out, not_16_out,
       not_17_out, not_18_out, not_19_out, not_20_out, not_21_out, not_22_out, not_23_out, not_25_out,
       not_26_out, not_27_out, not_28_out, not_29_out, not_30_out, not_31_out, not_32_out, not_33_out,
       not_34_out, not_35_out, not_36_out, not_37_out, not_38_out;

  not not_1 (not_1_out, in_1[3]);
  not not_2 (not_2_out, in_1[2]);
  not not_3 (not_3_out, in_2);
  not not_4 (not_4_out, in_1[4]);
  not not_5 (not_5_out, in_1[3]);
  not not_6 (not_6_out, in_1[2]);
  not not_7 (not_7_out, in_2);
  not not_8 (not_8_out, in_1[1]);
  not not_9 (not_9_out, in_1[3]);
  not not_10 (not_10_out, in_1[2]);
  not not_11 (not_11_out, in_2);
  not not_12 (not_12_out, in_1[1]);
  not not_13 (not_13_out, in_1[4]);
  not not_14 (not_14_out, in_1[3]);
  not not_15 (not_15_out, in_1[2]);
  not not_16 (not_16_out, in_1[4]);
  not not_17 (not_17_out, in_1[3]);
  not not_18 (not_18_out, in_1[2]);
  not not_19 (not_19_out, in_1[1]);
  not not_20 (not_20_out, in_1[3]);
  not not_21 (not_21_out, in_1[2]);
  not not_22 (not_22_out, in_1[1]);
  not not_23 (not_23_out, in_1[4]);
  and and_1 (and_1_out, not_1_out, not_2_out, not_3_out, not_4_out, in_1[1]);
  and and_2 (and_2_out, not_5_out, not_6_out, not_7_out, not_8_out, in_1[4]);
  and and_3 (and_3_out, not_9_out, not_10_out, not_11_out, not_12_out, not_13_out);
  and and_4 (and_4_out, not_14_out, not_15_out, in_2, not_16_out, in_1[1]);
  and and_5 (and_5_out, not_17_out, not_18_out, in_2, not_19_out, in_1[4]);
  and and_6 (and_6_out, not_20_out, not_21_out, in_2, not_22_out, not_23_out);
  or or_1 (out_3[1], and_1_out, and_2_out, and_3_out);
  or or_2 (out_3[2], and_4_out, and_5_out, and_6_out);
  not not_24 (out_3[0], 1'b1);
  not not_25 (not_25_out, in_1[3]);
  not not_26 (not_26_out, in_1[1]);
  not not_27 (not_27_out, in_2);
  not not_28 (not_28_out, in_1[4]);
  not not_29 (not_29_out, in_1[4]);
  not not_30 (not_30_out, in_1[2]);
  not not_31 (not_31_out, in_2);
  not not_32 (not_32_out, in_1[1]);
  not not_33 (not_33_out, in_1[3]);
  not not_34 (not_34_out, in_1[1]);
  not not_35 (not_35_out, in_1[4]);
  not not_36 (not_36_out, in_1[4]);
  not not_37 (not_37_out, in_1[2]);
  not not_38 (not_38_out, in_1[1]);
  and and_7 (and_7_out, not_25_out, not_26_out, not_27_out, not_28_out, in_1[2]);
  and and_8 (and_8_out, not_29_out, not_30_out, not_31_out, not_32_out, in_1[3]);
  and and_9 (and_9_out, not_33_out, not_34_out, in_2, not_35_out, in_1[2]);
  and and_10 (and_10_out, not_36_out, not_37_out, in_2, not_38_out, in_1[3]);
  or or_3 (out_3[4], and_7_out, and_8_out);
  or or_4 (out_3[3], and_9_out, and_10_out);

  // Other names for the same wires on the sheet: in = in_2; A1 = in_1[1]; A2 = in_1[2]; A3 = in_1[3]; A4 = in_1[4];
  //   B1 = out_3[1]; B2 = out_3[2]; B3 = out_3[3]; B4 = out_3[4]
endmodule
