// Logisim project 排序.circ as structural Verilog
module _1bit_swap (
  input  l1,
  input  l2,
  input  S,
  output O1,
  output O2
);

  wire and_1_out, and_2_out, and_3_out, and_4_out, not_1_out, not_2_out;

  not not_1 (not_1_out, S);
  not not_2 (not_2_out, S);
  and and_1 (and_1_out, l1, not_1_out);
  and and_2 (and_2_out, l2, S);
  and and_3 (and_3_out, l1, S);
  and and_4 (and_4_out, l2, not_2_out);
  or or_1 (O1, and_1_out, and_2_out);
  or or_2 (O2, and_3_out, and_4_out);
endmodule

module _4bit_swap (
  input  [3:0] in_1,
  input  [3:0] in_2,
  input  in_3,
  output [3:0] out_4,
  output [3:0] out_5
);

  _1bit_swap u_1bit_swap_1 (.l1(in_1[0]), .l2(in_2[0]), .S(in_3), .O1(out_4[0]), .O2(out_5[0]));
  _1bit_swap u_1bit_swap_2 (.l1(in_1[1]), .l2(in_2[1]), .S(in_3), .O1(out_4[1]), .O2(out_5[1]));
  _1bit_swap u_1bit_swap_3 (.l1(in_1[2]), .l2(in_2[2]), .S(in_3), .O1(out_4[2]), .O2(out_5[2]));
  _1bit_swap u_1bit_swap_4 (.l1(in_1[3]), .l2(in_2[3]), .S(in_3), .O1(out_4[3]), .O2(out_5[3]));
endmodule

module _4bit_sort (
  input  [3:0] A,
  input  [3:0] B,
  input  [3:0] C,
  input  [3:0] D,
  output [3:0] out_5,
  output [3:0] _1,
  output [3:0] out_7,
  output [3:0] _2,
  output [3:0] _3,
  output [3:0] _4
);

  wire comparator_1_lt, comparator_2_lt, comparator_3_lt, comparator_4_lt, comparator_5_lt, comparator_6_lt;
  wire [3:0] A2, B2, C1, C2, D1, D2;

  Comparator #(.width(4), .mode("unsigned")) comparator_1 (.a(A), .b(B), .lt(comparator_1_lt));  // open: gt, eq
  Comparator #(.width(4), .mode("unsigned")) comparator_2 (.a(out_5), .b(C), .lt(comparator_2_lt));  // open: gt, eq
  Comparator #(.width(4), .mode("unsigned")) comparator_3 (.a(A2), .b(D), .lt(comparator_3_lt));  // open: gt, eq
  Comparator #(.width(4), .mode("unsigned")) comparator_4 (.a(out_7), .b(C1), .lt(comparator_4_lt));  // open: gt, eq
  Comparator #(.width(4), .mode("unsigned")) comparator_5 (.a(B2), .b(D1), .lt(comparator_5_lt));  // open: gt, eq
  Comparator #(.width(4), .mode("unsigned")) comparator_6 (.a(C2), .b(D2), .lt(comparator_6_lt));  // open: gt, eq
  _4bit_swap u_4bit_swap_1 (.in_1(A), .in_2(B), .in_3(comparator_1_lt), .out_4(out_5), .out_5(out_7));
  _4bit_swap u_4bit_swap_2 (.in_1(out_5), .in_2(C), .in_3(comparator_2_lt), .out_4(A2), .out_5(C1));
  _4bit_swap u_4bit_swap_3 (.in_1(A2), .in_2(D), .in_3(comparator_3_lt), .out_4(_4), .out_5(D1));
  _4bit_swap u_4bit_swap_4 (.in_1(out_7), .in_2(C1), .in_3(comparator_4_lt), .out_4(B2), .out_5(C2));
  _4bit_swap u_4bit_swap_5 (.in_1(B2), .in_2(D1), .in_3(comparator_5_lt), .out_4(_3), .out_5(D2));
  _4bit_swap u_4bit_swap_6 (.in_1(C2), .in_2(D2), .in_3(comparator_6_lt), .out_4(_2), .out_5(_1));

  // Other names for the same wires on the sheet: A1[3:0] = out_5; A3[3:0] = _4; B1[3:0] = out_7; B3[3:0] = _3;
  //   C3[3:0] = _2; D3[3:0] = _1
endmodule
