// Logisim project 斐波那契数列(矩阵幂算法）.circ as structural Verilog: 5 circuits, main circuit main
module main (
  input  [31:0] N,
  output [31:0] Nth
);

  wire A, clock_1_out, clock_2_out, comparator_2_eq, comparator_3_gt, multiplexer_1_out, not_1_out;
  wire [4:0] counter_1_q, register_1_q;
  wire [5:0] adder_1_out, counter_2_q, register_2_q;
  wire [31:0] fab_1_nth, multiplexer_2_out, register_3_q, subtractor_1_out;

  Comparator #(.width(32)) comparator_1 (.a({32{1'b0}}), .b(N), .eq(A));  // open: gt, lt
  Subtractor #(.width(32)) subtractor_1 (.a(N), .b(32'h1), .out(subtractor_1_out));  // open: bin, bout
  Counter #(.width(5), .max('h1f)) counter_1 (.Q(counter_1_q), .clk(clock_1_out));  // open: load, D, count, carry, clr
  Register #(.width(5)) register_1 (.D(counter_1_q), .Q(register_1_q), .clk(clock_1_out));  // open: en, clr
  fab fab_1 (.Nth(fab_1_nth), .in_1(multiplexer_1_out));
  Multiplexer #(.select(5)) multiplexer_1 (
    .in0(subtractor_1_out[31]), .in1(subtractor_1_out[30]), .in2(subtractor_1_out[29]),
    .in3(subtractor_1_out[28]), .in4(subtractor_1_out[27]), .in5(subtractor_1_out[26]),
    .in6(subtractor_1_out[25]), .in7(subtractor_1_out[24]), .in8(subtractor_1_out[23]),
    .in9(subtractor_1_out[22]), .in10(subtractor_1_out[21]), .in11(subtractor_1_out[20]),
    .in12(subtractor_1_out[19]), .in13(subtractor_1_out[18]), .in14(subtractor_1_out[17]),
    .in15(subtractor_1_out[16]), .in16(subtractor_1_out[15]), .in17(subtractor_1_out[14]),
    .in18(subtractor_1_out[13]), .in19(subtractor_1_out[12]), .in20(subtractor_1_out[11]),
    .in21(subtractor_1_out[10]), .in22(subtractor_1_out[9]), .in23(subtractor_1_out[8]),
    .in24(subtractor_1_out[7]), .in25(subtractor_1_out[6]), .in26(subtractor_1_out[5]),
    .in27(subtractor_1_out[4]), .in28(subtractor_1_out[3]), .in29(subtractor_1_out[2]),
    .in30(subtractor_1_out[1]), .in31(subtractor_1_out[0]), .out(multiplexer_1_out), .sel(register_1_q));  // open: en
  Adder #(.width(6)) adder_1 (.a(6'b000001), .b(register_2_q), .out(adder_1_out));  // open: cin, cout
  Register #(.width(6)) register_2 (.D(adder_1_out), .Q(register_2_q), .clk(clock_1_out));  // open: en, clr
  Clock clock_1 (.out(clock_1_out));
  Multiplexer #(.width(32)) multiplexer_2 (
    .in0(fab_1_nth), .in1({32{1'b0}}), .out(multiplexer_2_out), .sel(A));  // open: en
  Clock clock_2 (.out(clock_2_out));
  Comparator #(.width(6)) comparator_2 (.a(6'b100000), .b(register_2_q), .eq(comparator_2_eq));  // open: gt, lt
  Register #(.width(32)) register_3 (
    .D(multiplexer_2_out), .en(comparator_2_eq), .Q(register_3_q), .clk(clock_2_out));  // open: clr
  Counter #(.width(6), .max('h3f)) counter_2 (.Q(counter_2_q), .clk(clock_1_out));  // open: load, D, count, carry, clr
  Register #(.width(32)) register_4 (.D(register_3_q), .en(not_1_out), .Q(Nth), .clk(clock_2_out));  // open: clr
  not not_1 (not_1_out, comparator_3_gt);
  Comparator #(.width(6)) comparator_3 (.a(counter_2_q), .b(6'b011111), .gt(comparator_3_gt));  // open: eq, lt
endmodule

module fab (
  input  in_1,
  output [31:0] Nth
);

  wire clock_1_out;
  wire [31:0] A, A0, A2, A3, A_prime, B, B0, B2, B3, C, C0, C2, C3, D, D0, D2, D3, D_prime;

  initial_1 initial_1_1 (.\input (A_prime), .\output (A));
  Register #(.width(32)) u_A (.D(A), .Q(A0), .clk(clock_1_out));  // open: en, clr
  Register #(.width(32)) u_B (.D(B), .Q(B0), .clk(clock_1_out));  // open: en, clr
  Register #(.width(32)) u_C (.D(C), .Q(C0), .clk(clock_1_out));  // open: en, clr
  Register #(.width(32)) u_D (.D(D), .Q(D0), .clk(clock_1_out));  // open: en, clr
  Clock clock_1 (.out(clock_1_out));
  initial_1 initial_1_2 (.\input (D_prime), .\output (D));
  input_0 input_0_1 (.preA(A0), .preB(B0), .preC(C0), .preD(D0), .A(A2), .B(B2), .C(C2), .D(D2));
  input_1 input_1_1 (.preA(A0), .preB(B0), .preC(C0), .preD(D0), .C(A3), .D(B3), .C_2(C3), .D_2(D3));
  Multiplexer #(.width(32)) multiplexer_1 (.in0(A2), .in1(A3), .out(A_prime), .sel(in_1));  // open: en
  Multiplexer #(.width(32)) multiplexer_2 (.in0(B2), .in1(B3), .out(B), .sel(in_1));  // open: en
  Multiplexer #(.width(32)) multiplexer_3 (.in0(C2), .in1(C3), .out(C), .sel(in_1));  // open: en
  Multiplexer #(.width(32)) multiplexer_4 (.in0(D2), .in1(D3), .out(D_prime), .sel(in_1));  // open: en

  // Other names for the same wires on the sheet: A1[31:0] = Nth
endmodule

module input_1 (
  input  [31:0] preA,
  input  [31:0] preB,
  input  [31:0] preC,
  input  [31:0] preD,
  output [31:0] C,
  output [31:0] D,
  output [31:0] C_2,
  output [31:0] D_2
);

  wire [31:0] adder_1_out, adder_2_out, adder_3_out, adder_4_out, multiplier_1_out, multiplier_2_out,
       multiplier_3_out, multiplier_4_out, multiplier_5_out, multiplier_6_out, multiplier_7_out,
       multiplier_8_out, multiplier_9_out, multiplier_10_out, multiplier_11_out, multiplier_12_out;

  Multiplier #(.width(32)) multiplier_1 (.a(preA), .b(preA), .out(multiplier_1_out));  // open: cin, cout
  Multiplier #(.width(32)) multiplier_2 (.a(preB), .b(preC), .out(multiplier_2_out));  // open: cin, cout
  Multiplier #(.width(32)) multiplier_3 (.a(preA), .b(preB), .out(multiplier_3_out));  // open: cin, cout
  Multiplier #(.width(32)) multiplier_4 (.a(preB), .b(preD), .out(multiplier_4_out));  // open: cin, cout
  Multiplier #(.width(32)) multiplier_5 (.a(preA), .b(preA), .out(multiplier_5_out));  // open: cin, cout
  Multiplier #(.width(32)) multiplier_6 (.a(preB), .b(preC), .out(multiplier_6_out));  // open: cin, cout
  Multiplier #(.width(32)) multiplier_7 (.a(preA), .b(preC), .out(multiplier_7_out));  // open: cin, cout
  Multiplier #(.width(32)) multiplier_8 (.a(preC), .b(preD), .out(multiplier_8_out));  // open: cin, cout
  Multiplier #(.width(32)) multiplier_9 (.a(preB), .b(preC), .out(multiplier_9_out));  // open: cin, cout
  Multiplier #(.width(32)) multiplier_10 (.a(preD), .b(preD), .out(multiplier_10_out));  // open: cin, cout
  Multiplier #(.width(32)) multiplier_11 (.a(preA), .b(preC), .out(multiplier_11_out));  // open: cin, cout
  Multiplier #(.width(32)) multiplier_12 (.a(preC), .b(preD), .out(multiplier_12_out));  // open: cin, cout
  Adder #(.width(32)) adder_1 (.a(multiplier_1_out), .b(multiplier_2_out), .out(adder_1_out));  // open: cin, cout
  Adder #(.width(32)) adder_2 (.a(multiplier_3_out), .b(multiplier_4_out), .out(adder_2_out));  // open: cin, cout
  Adder #(.width(32)) adder_3 (.a(multiplier_7_out), .b(multiplier_8_out), .out(adder_3_out));  // open: cin, cout
  Adder #(.width(32)) adder_4 (.a(multiplier_9_out), .b(multiplier_10_out), .out(adder_4_out));  // open: cin, cout
  Adder #(.width(32)) adder_5 (.a(adder_1_out), .b(adder_2_out), .out(C));  // open: cin, cout
  Adder #(.width(32)) adder_6 (.a(multiplier_5_out), .b(multiplier_6_out), .out(D));  // open: cin, cout
  Adder #(.width(32)) adder_7 (.a(adder_3_out), .b(adder_4_out), .out(C_2));  // open: cin, cout
  Adder #(.width(32)) adder_8 (.a(multiplier_11_out), .b(multiplier_12_out), .out(D_2));  // open: cin, cout

  // Other names for the same wires on the sheet: A[31:0] = preA; B[31:0] = preB; C_t[31:0] = preC; D_t[31:0] = preD
endmodule

module input_0 (
  input  [31:0] preA,
  input  [31:0] preB,
  input  [31:0] preC,
  input  [31:0] preD,
  output [31:0] A,
  output [31:0] B,
  output [31:0] C,
  output [31:0] D
);

  wire [31:0] multiplier_1_out, multiplier_2_out, multiplier_3_out, multiplier_4_out, multiplier_5_out,
       multiplier_6_out, multiplier_7_out, multiplier_8_out;

  Multiplier #(.width(32)) multiplier_1 (.a(preA), .b(preA), .out(multiplier_1_out));  // open: cin, cout
  Multiplier #(.width(32)) multiplier_2 (.a(preB), .b(preC), .out(multiplier_2_out));  // open: cin, cout
  Multiplier #(.width(32)) multiplier_3 (.a(preA), .b(preB), .out(multiplier_3_out));  // open: cin, cout
  Multiplier #(.width(32)) multiplier_4 (.a(preB), .b(preD), .out(multiplier_4_out));  // open: cin, cout
  Multiplier #(.width(32)) multiplier_5 (.a(preA), .b(preC), .out(multiplier_5_out));  // open: cin, cout
  Multiplier #(.width(32)) multiplier_6 (.a(preC), .b(preD), .out(multiplier_6_out));  // open: cin, cout
  Multiplier #(.width(32)) multiplier_7 (.a(preB), .b(preC), .out(multiplier_7_out));  // open: cin, cout
  Multiplier #(.width(32)) multiplier_8 (.a(preD), .b(preD), .out(multiplier_8_out));  // open: cin, cout
  Adder #(.width(32)) adder_1 (.a(multiplier_1_out), .b(multiplier_2_out), .out(A));  // open: cin, cout
  Adder #(.width(32)) adder_2 (.a(multiplier_3_out), .b(multiplier_4_out), .out(B));  // open: cin, cout
  Adder #(.width(32)) adder_3 (.a(multiplier_5_out), .b(multiplier_6_out), .out(C));  // open: cin, cout
  Adder #(.width(32)) adder_4 (.a(multiplier_7_out), .b(multiplier_8_out), .out(D));  // open: cin, cout

  // Other names for the same wires on the sheet: A_t[31:0] = preA; B_t[31:0] = preB; C_t[31:0] = preC;
  //   D_t[31:0] = preD
endmodule

module initial_1 (
  input  [31:0] \input ,
  output [31:0] \output 
);

  wire clock_1_out, register_1_q;

  Register #(.width(1)) register_1 (.D(1'b1), .Q(register_1_q), .clk(clock_1_out));  // open: en, clr
  Clock clock_1 (.out(clock_1_out));
  Multiplexer #(.width(32)) multiplexer_1 (.in0(32'h1), .in1(\input ), .out(\output ), .sel(register_1_q));  // open: en
endmodule
