// Logisim project 斐波那契数列.circ as structural Verilog: 1 circuit, main circuit main
module main (
  input  [2:0] in_1,
  output [3:0] out_2
);

  wire and_2_out, C, clock_1_out, comparator_1_lt, \end , not_1_out, not_2_out, not_3_out, not_4_out,
       not_5_out, not_6_out, not_7_out;
  wire [2:0] count;
  wire [3:0] A, B, multiplexer_1_out, multiplexer_2_out, Q1, Q2, register_3_q;

  Multiplexer #(.width(4)) multiplexer_1 (.in0(A), .in1(4'b0001), .out(multiplexer_1_out), .sel(C));  // open: en
  Register #(.width(4)) register_1 (.D(multiplexer_1_out), .en(not_1_out), .Q(Q1), .clk(clock_1_out));  // open: clr
  not not_1 (not_1_out, \end );
  Adder #(.width(4)) adder_1 (.a(Q1), .b(Q2), .out(A));  // open: cin, cout
  Multiplexer #(.width(4)) multiplexer_2 (.in0(B), .in1(4'b0000), .out(multiplexer_2_out), .sel(C));  // open: en
  Register #(.width(4)) register_2 (.D(multiplexer_2_out), .en(not_2_out), .Q(Q2), .clk(clock_1_out));  // open: clr
  not not_2 (not_2_out, \end );
  Clock clock_1 (.out(clock_1_out));
  Comparator #(.width(4), .mode("unsigned")) comparator_1 (.a(Q1), .b(Q2), .lt(comparator_1_lt));  // open: gt, eq
  Multiplexer #(.width(4)) multiplexer_3 (.in0(Q1), .in1(Q2), .out(B), .sel(comparator_1_lt));  // open: en
  Counter #(.width(3), .max('h7)) counter_1 (.Q(count), .clk(clock_1_out));  // open: load, D, count, carry, clr
  and and_1 (C, not_5_out, not_3_out, not_4_out);
  not not_3 (not_3_out, count[1]);
  not not_4 (not_4_out, count[0]);
  not not_5 (not_5_out, count[2]);
  Comparator #(.width(3), .mode("unsigned")) comparator_2 (.a(count), .b(in_1), .eq(\end ));  // open: gt, lt
  Register #(.width(4)) register_3 (.D(A), .Q(register_3_q), .clk(\end ));  // open: en, clr
  Multiplexer #(.width(4)) multiplexer_4 (.in0(register_3_q), .in1(4'b0001), .out(out_2), .sel(and_2_out));  // open: en
  and and_2 (and_2_out, not_6_out, not_7_out, in_1[0]);
  not not_6 (not_6_out, in_1[2]);
  not not_7 (not_7_out, in_1[1]);

  // Other names for the same wires on the sheet: in[2:0] = in_1
endmodule
